// Logisim project SRLatch.circ as structural Verilog: 2 circuits, main circuit SRLatch
module SRLatch (
  input  in_1,
  input  in_2,
  output out_3,
  output out_4
);

  or or_1 (out_3, in_1, out_4);
  or or_2 (out_4, in_2, out_3);
endmodule

module Dlatch (
  input  D,
  input  Strobe,
  output not_Q,
  output Q
);

  wire and_1_out, and_2_out, not_1_out;

  not not_1 (not_1_out, D);
  and and_1 (and_1_out, D, Strobe);
  and and_2 (and_2_out, not_1_out, Strobe);
  SRLatch srlatch_1 (.in_1(and_1_out), .in_2(and_2_out), .out_3(not_Q), .out_4(Q));
endmodule
