// Logisim project memory.circ as structural Verilog: 4 circuits, main circuit S-R Latch
module S_R_Latch (
  input  S,
  input  R,
  output not_Q,
  output Q
);

  nor nor_1 (not_Q, S, Q);
  nor nor_2 (Q, not_Q, R);
endmodule

module D_Latch (
  input  D,
  input  Strobe,
  output Q
);

  wire and_1_out, and_2_out, not_1_out;

  not not_1 (not_1_out, D);
  and and_1 (and_1_out, D, Strobe);
  and and_2 (and_2_out, not_1_out, Strobe);
  S_R_Latch s_r_latch_1 (.S(and_1_out), .R(and_2_out), .Q(Q));  // open: not_Q

  // Notes on the sheet:
  //   S
  //   R
endmodule

module _2_bit_decoder (
  input  Input1,
  input  Input0,
  output Output0,
  output Output1,
  output Output2,
  output Output3
);

  wire not_1_out, not_2_out;

  not not_1 (not_1_out, Input1);
  not not_2 (not_2_out, Input0);
  and and_1 (Output0, not_1_out, not_2_out);
  and and_2 (Output1, not_1_out, Input0);
  and and_3 (Output2, Input1, not_2_out);
  and and_4 (Output3, Input1, Input0);
endmodule

module _12_nGb_memory (
  input  Bit_1,
  input  Bit_0,
  input  Data_Bits__In,
  input  in_4,
  input  in_5,
  input  Write_Enabled,
  output out_7,
  output Data_Bits__Out,
  output out_9
);

  wire and_1_out, and_2_out, and_3_out, and_4_out, and_5_out, and_6_out, and_7_out, and_8_out, and_9_out,
       and_10_out, and_11_out, and_12_out, and_13_out, and_14_out, and_15_out, and_16_out, D_Latch_2_q,
       D_Latch_3_q, D_Latch_4_q, D_Latch_5_q, D_Latch_6_q, D_Latch_7_q, D_Latch_8_q, D_Latch_9_q,
       D_Latch_10_q, D_Latch_11_q, D_Latch_12_q, D_Latch_q, Decoder_output0, Decoder_output1,
       Decoder_output2, Decoder_output3;

  _2_bit_decoder Decoder (
    .Input1(Bit_1), .Input0(Bit_0), .Output0(Decoder_output0), .Output1(Decoder_output1),
    .Output2(Decoder_output2), .Output3(Decoder_output3));
  and and_1 (and_1_out, Decoder_output0, Write_Enabled);
  and and_2 (and_2_out, Decoder_output1, Write_Enabled);
  and and_3 (and_3_out, Decoder_output2, Write_Enabled);
  and and_4 (and_4_out, Decoder_output3, Write_Enabled);
  D_Latch D_Latch (.D(in_4), .Strobe(and_1_out), .Q(D_Latch_q));
  D_Latch D_Latch_2 (.D(Data_Bits__In), .Strobe(and_1_out), .Q(D_Latch_2_q));
  D_Latch D_Latch_3 (.D(Data_Bits__In), .Strobe(and_2_out), .Q(D_Latch_3_q));
  D_Latch D_Latch_4 (.D(in_4), .Strobe(and_2_out), .Q(D_Latch_4_q));
  D_Latch D_Latch_5 (.D(Data_Bits__In), .Strobe(and_3_out), .Q(D_Latch_5_q));
  D_Latch D_Latch_6 (.D(in_4), .Strobe(and_3_out), .Q(D_Latch_6_q));
  D_Latch D_Latch_7 (.D(in_4), .Strobe(and_4_out), .Q(D_Latch_7_q));
  D_Latch D_Latch_8 (.D(Data_Bits__In), .Strobe(and_4_out), .Q(D_Latch_8_q));
  D_Latch D_Latch_9 (.D(in_5), .Strobe(and_1_out), .Q(D_Latch_9_q));
  D_Latch D_Latch_10 (.D(in_5), .Strobe(and_2_out), .Q(D_Latch_10_q));
  D_Latch D_Latch_11 (.D(in_5), .Strobe(and_3_out), .Q(D_Latch_11_q));
  D_Latch D_Latch_12 (.D(in_5), .Strobe(and_4_out), .Q(D_Latch_12_q));
  and and_5 (and_5_out, D_Latch_2_q, Decoder_output0);
  and and_6 (and_6_out, D_Latch_q, Decoder_output0);
  and and_7 (and_7_out, D_Latch_9_q, Decoder_output0);
  and and_8 (and_8_out, D_Latch_3_q, Decoder_output1);
  and and_9 (and_9_out, D_Latch_4_q, Decoder_output1);
  and and_10 (and_10_out, D_Latch_10_q, Decoder_output1);
  and and_11 (and_11_out, D_Latch_5_q, Decoder_output2);
  and and_12 (and_12_out, D_Latch_6_q, Decoder_output2);
  and and_13 (and_13_out, D_Latch_11_q, Decoder_output2);
  and and_14 (and_14_out, D_Latch_8_q, Decoder_output3);
  and and_15 (and_15_out, D_Latch_7_q, Decoder_output3);
  and and_16 (and_16_out, D_Latch_12_q, Decoder_output3);
  or or_1 (out_7, and_5_out, and_8_out, and_11_out, and_14_out);
  or or_2 (out_9, and_7_out, and_10_out, and_13_out, and_16_out);
  or or_3 (Data_Bits__Out, and_6_out, and_9_out, and_12_out, and_15_out);

  // Notes on the sheet:
  //   Address
endmodule
